# Fritzing sketch schmetic (saved by Fritzing 0.9.3b)

parts:
  J1 = STM32 Nucleo boards
  부품1 = Soil Moisture Sensor
  Mod1 = KY-019 5V Relay Module [package="Breakout board"]
  M1 = Humidity and Temperature Sensor DHT11
  WATER_PUMP2 = water pump/motor  # not connected
  J2 = Power Jack [package=power_jack_combo]
  부품2 = 12 NeoPixel Ring [part_number=1643]
  U1 = Nokia 6100 Color LCD [package=nokia6100_lcd]
  F1 = Small Fan, based on Fan - Ventilador [package=THT]
  U2 = ESP8266 ESP-01 Upgraded WiFi Module [part_number=ESP8266]

nets:
  N1: J1.A0, 부품1.SIG
  N2: J1.A1, M1.Data
  N3: J1.PC11, U2.TXD
  N4: J1.D8, U1.SCK
  N5: J1.D9_PWM, 부품2.OUT
  N6: J1.D10_PWM/SS, F1.5V
  N7: J1.D4, Mod1.S
  N8: J1.D6_PWM, U1.DIO
  3V3: J1.3V3, U2.VCC, U2.CH_PD
  GND: J1.GND, 부품1.GND, Mod1.-, Mod1.Common, M1.GND, J2.GND, 부품2.GND, U1.RESET, F1.GND, U2.GND
  N9: J1.PC10, U2.RXD
  VCC: 부품1.VCC, Mod1.+, M1.Vcc, J2.GNDBREAK, 부품2.VDD, U1.VDIGITAL

custom parts:
  KY-019 5V Relay Module: KY-019 5V Relay module, used to control AC circuits. (Special thanks to vanepp for fixing the PCB holes and other errors)
  Humidity and Temperature Sensor DHT11: Digital relative humidity & temperature sensor DHT11
  water pump/motor: WATER PUMP BY ARDUBLOCKTR
  12 NeoPixel Ring: 12 ultra bright smart LED NeoPixels are arranged in a circle with 1.5" (37mm) outer diameter. The rings are 'chainable' - connect the output pin of one to the input pin of another. Use only one microcontroller pin to control as many as you can chain together! Each LED is addressable as the driver chip is inside the LED. Each one has ~18mA constant current drive so the color will be very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
  Small Fan, based on Fan - Ventilador: Small 2-pin fan, commonly used with single-board computers, 3d-printers, etc. This work is based on a much larger fan, as commonly found in desktop computers
  ESP8266 ESP-01 Upgraded WiFi Module: Upgraded Version ESP-01,all Flash are upgraded to 1M byte.Also support Cloud service remote transmission.
